# Fritzing sketch setting (saved by Fritzing 0.9.3b)
breadboards: 1

parts:
  パーツ1 = Arduino Uno (Rev3)
  S1 = Pushbutton [package="[THT]"]
  R1 = Resistor [tolerance=±5% resistance=1k package=THT]
  R2 = Resistor [tolerance=±5% resistance=1k package=THT]
  LED1 = LED - 5mm [color="Red (633nm)" package="5 mm [THT]"]

nets:
  N1: パーツ1.D2, S1.Pin_3, S1.Pin_4, R1.Pin_1
  N2: パーツ1.D3_PWM, LED1.anode
  N3: パーツ1.5V, S1.Pin_1, S1.Pin_2
  N4: パーツ1.GND, R1.Pin_0, R2.Pin_1
  N5: R2.Pin_0, LED1.cathode
